# Fritzing sketch Untitled Sketch 2 (saved by Fritzing 1.0.2b)
breadboards: 1

parts:
  M1 = DOIT Esp32 DevKit v1 (30 pins long, 11 pins width) [part_number=ESP32S-PIN30]
  M2 = DHT11-Grove-Temperature-Sensor_1
  パーツ1 = Soil Moisture Sensor

nets:
  GND: M1.GND, M2.connector3, パーツ1.GND
  N1: M1.D32, M2.connector0
  N2: M1.D33, パーツ1.SIG
  VIN: M1.VIN, M2.connector2, パーツ1.VCC

custom parts:
  DOIT Esp32 DevKit v1 (30 pins long, 11 pins width): The DOIT Esp32 DevKit v1 is one of the development board created by DOIT to evaluate the ESP-WROOM-32 module. It is based on the ESP32 microcontroller that boasts Wifi, Bluetooth, Ethernet and Low Power support all in a single chip. (vanepp) made breadboard work, adjusted pin numbering and labels and reduced size of schematic and cleaned up pcb. This chip is 30pins long (2 x15) and 11 pins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
